// Logisim project cpu.circ as structural Verilog: 1 circuit, main circuit main
module main (
  input  clock_run,
  input  clock_halt,
  input  in_3,
  input  in_4,
  input  [7:0] data_in,
  input  [15:0] addr_in,
  input  ip_to_addr,
  input  ip_hi_to_data,
  input  ip_lo_to_data,
  input  ip_inc,
  input  data_to_ip_lo,
  input  data_to_ip_hi,
  input  addr_to_ip,
  input  data_to_ir,
  input  mar_hi_to_data,
  input  mar_lo_to_data,
  input  mar_inc,
  input  data_to_mar_lo,
  input  data_to_mar_hi,
  input  addr_to_mar,
  input  data_to_ram,
  input  ram_to_data,
  output clock_halt_2,
  output clock_inv,
  output clock,
  output [7:0] data,
  output [15:0] addr,
  output [15:0] ip,
  output [7:0] ip_lo,
  output [7:0] ip_hi,
  output [7:0] out_31,
  output [15:0] mar,
  output [7:0] ip_lo_2,
  output [7:0] ip_hi_2,
  output out_35
);

  wire and_1_out, and_2_out, and_3_out, and_4_out, and_5_out, and_6_out, and_8_out, and_9_out, clock_1_out,
       clock_step_out, counter_3_carry, counter_4_carry, counter_5_carry, counter_6_carry, counter_7_carry,
       counter_8_carry, ip_reset_out, nor_1_out, nor_2_out, nor_3_out, nor_4_out, nor_5_out, nor_6_out,
       not_1_out, not_2_out, not_3_out, or_1_out, or_2_out, or_3_out, or_4_out, or_5_out, or_6_out, or_7_out,
       or_8_out, or_9_out, or_10_out, or_11_out;
  wire [3:0] controlled_buffer_5_out, controlled_buffer_9_out;
  wire [7:0] ram_1_data;
  wire [15:4] controlled_buffer_5_out_2, controlled_buffer_9_out_2;

  assign data = in_3 ? data_in : 8'bz;  // Controlled_Buffer controlled_buffer_1
  assign data = ip_hi_to_data ? ip[15:8] : 8'bz;  // Controlled_Buffer controlled_buffer_2
  assign data = ip_lo_to_data ? ip[7:0] : 8'bz;  // Controlled_Buffer controlled_buffer_3
  Counter #(.width(4), .max('hf)) counter_1 (
    .load(or_3_out), .D(controlled_buffer_5_out_2[15:12]), .count(ip_inc), .Q(ip[15:12]), .clk(or_1_out),
    .clr(ip_reset_out));  // open: carry
  or or_1 (or_1_out, nor_1_out, and_1_out);
  assign controlled_buffer_5_out_2[15:8] = data_to_ip_hi ? data : 8'bz;  // Controlled_Buffer controlled_buffer_4
  assign {controlled_buffer_5_out_2[7:4], controlled_buffer_5_out} = data_to_ip_lo ? data : 8'bz;  // Controlled_Buffer controlled_buffer_5
  assign data = mar_hi_to_data ? ip_hi_2 : 8'bz;  // Controlled_Buffer controlled_buffer_6
  assign data = mar_lo_to_data ? ip_lo_2 : 8'bz;  // Controlled_Buffer controlled_buffer_7
  Counter #(.width(4), .max('hf)) counter_2 (
    .load(or_5_out), .D(controlled_buffer_9_out_2[15:12]), .count(mar_inc), .Q(ip_hi_2[7:4]), .clk(or_2_out));  // open: carry, clr
  or or_2 (or_2_out, nor_2_out, and_2_out);
  assign controlled_buffer_9_out_2[15:8] = data_to_mar_hi ? data : 8'bz;  // Controlled_Buffer controlled_buffer_8
  assign {controlled_buffer_9_out_2[7:4], controlled_buffer_9_out} = data_to_mar_lo ? data : 8'bz;  // Controlled_Buffer controlled_buffer_9
  not not_1 (not_1_out, data_to_ram);
  assign data = ram_to_data ? ram_1_data : 8'bz;  // Controlled_Buffer controlled_buffer_10
  nor nor_1 (nor_1_out, counter_3_carry, or_3_out);
  nor nor_2 (nor_2_out, counter_4_carry, or_5_out);
  Button clock_step (.out(clock_step_out));
  and and_1 (and_1_out, or_3_out, clock);
  or or_3 (or_3_out, data_to_ip_hi, addr_to_ip);
  or or_4 (or_4_out, data_to_ip_lo, addr_to_ip);
  and and_2 (and_2_out, or_5_out, clock);
  or or_5 (or_5_out, data_to_mar_hi, addr_to_mar);
  or or_6 (or_6_out, data_to_mar_lo, addr_to_mar);
  Clock clock_1 (.out(clock_1_out));
  not not_2 (not_2_out, clock_run);
  Counter #(.width(4), .max('hf)) counter_3 (
    .load(or_3_out), .D(controlled_buffer_5_out_2[11:8]), .count(ip_inc), .Q(ip[11:8]),
    .carry(counter_3_carry), .clk(or_7_out), .clr(ip_reset_out));
  Register register_1 (.D(data), .en(data_to_ir), .Q(out_31), .clk(clock));  // open: clr
  Counter #(.width(4), .max('hf)) counter_4 (
    .load(or_5_out), .D(controlled_buffer_9_out_2[11:8]), .count(mar_inc), .Q(ip_hi_2[3:0]),
    .carry(counter_4_carry), .clk(or_8_out));  // open: clr
  and and_3 (and_3_out, clock_1_out, clock_run);
  and and_4 (and_4_out, not_2_out, clock_step_out);
  not not_3 (not_3_out, clock_halt);
  or or_7 (or_7_out, nor_3_out, and_5_out);
  or or_8 (or_8_out, nor_4_out, and_6_out);
  or or_9 (or_9_out, and_3_out, and_4_out);
  nor nor_3 (nor_3_out, counter_5_carry, or_3_out);
  and and_5 (and_5_out, or_3_out, clock);
  nor nor_4 (nor_4_out, counter_6_carry, or_5_out);
  and and_6 (and_6_out, or_5_out, clock);
  and and_7 (clock, or_9_out, not_3_out);
  not not_4 (clock_inv, clock);
  Counter #(.width(4), .max('hf)) counter_5 (
    .load(or_4_out), .D(controlled_buffer_5_out_2[7:4]), .count(ip_inc), .Q(ip[7:4]),
    .carry(counter_5_carry), .clk(or_10_out), .clr(ip_reset_out));
  or or_10 (or_10_out, nor_5_out, and_8_out);
  Counter #(.width(4), .max('hf)) counter_6 (
    .load(or_6_out), .D(controlled_buffer_9_out_2[7:4]), .count(mar_inc), .Q(ip_lo_2[7:4]),
    .carry(counter_6_carry), .clk(or_11_out));  // open: clr
  or or_11 (or_11_out, nor_6_out, and_9_out);
  nor nor_5 (nor_5_out, counter_7_carry, or_4_out);
  and and_8 (and_8_out, or_4_out, clock);
  nor nor_6 (nor_6_out, counter_8_carry, or_6_out);
  and and_9 (and_9_out, or_6_out, clock);
  RAM #(.addrWidth(16)) ram_1 (
    .addr({ip_hi_2, ip_lo_2}), .data(ram_1_data), .sel(1'b1), .clk(clock), .ld(not_1_out));  // open: clr
  Counter #(.width(4), .max('hf)) counter_7 (
    .load(or_4_out), .D(controlled_buffer_5_out), .count(ip_inc), .Q(ip[3:0]), .carry(counter_7_carry),
    .clk(clock), .clr(ip_reset_out));
  Counter #(.width(4), .max('hf)) counter_8 (
    .load(or_6_out), .D(controlled_buffer_9_out), .count(mar_inc), .Q(ip_lo_2[3:0]), .carry(counter_8_carry),
    .clk(clock));  // open: clr
  assign addr = in_4 ? addr_in : 16'bz;  // Controlled_Buffer controlled_buffer_11
  assign addr = ip_to_addr ? ip : 16'bz;  // Controlled_Buffer controlled_buffer_12
  assign {controlled_buffer_5_out_2, controlled_buffer_5_out} = addr_to_ip ? addr : 16'bz;  // Controlled_Buffer controlled_buffer_13
  assign {controlled_buffer_9_out_2, controlled_buffer_9_out} = addr_to_mar ? addr : 16'bz;  // Controlled_Buffer controlled_buffer_14
  Button ip_reset (.out(ip_reset_out));

  assign clock_halt_2 = clock_halt;
  assign ip_hi = ip[15:8];
  assign ip_lo = ip[7:0];
  assign mar = {ip_hi_2, ip_lo_2};

  // Notes on the sheet:
  //   8-Bit Data Bus
  //   Program Counter
  //   Random Access Memory
  //   Clock
  //   Instruction Register
  //   Memory Address Register
  //   16-Bit Address Bus
  //   Instruction Pointer
endmodule
